# Fritzing sketch Ada (saved by Fritzing 0.9.3b)
circuit board: 10.0147cm x 5.41049cm
breadboards: 1

parts:
  Part2 = InvenSense MPU6050
  U1 = ESP32S-HiLetgo [part_number=ESP32S-HiLetgo]
  U2 = SWITCH_SPDT [package=kps-1290]
  M1 = Stepper Motor - Bipolar
  Mod2 = TMC2209 [package=THT]
  Mod3 = TMC2209 [package=THT]
  R1 = Resistor [tolerance=±5% resistance=1k package="0402 [SMD]"]
  M2 = Stepper Motor - Bipolar
  C3 = Electrolytic Capacitor [capacitance=100µF voltage=25V package="100 mil [THT, electrolytic]"]
  C4 = Electrolytic Capacitor [capacitance=100µF voltage=25V package="100 mil [THT, electrolytic]"]
  Part3 = Lithium Ion Polymer Battery 3.7v 2500mAh [part_number=328]
  C9 = Ceramic Capacitor [capacitance=0.1µF package="200 mil [THT, multilayer]"]
  JP1 = Header 5x2 [part_number="JTAG Debugger" package=2x5-ra]
  C14 = Ceramic Capacitor [capacitance=0.1µF package="200 mil [THT, multilayer]"]
  C13 = Ceramic Capacitor [capacitance=0.1µF package="200 mil [THT, multilayer]"]
  C8 = Ceramic Capacitor [capacitance=0.1µF package="200 mil [THT, multilayer]"]
  A1 = MP2315
  U3 = LM386 [package=dip08]
  R2 = Resistor [tolerance=±5% resistance=10k package="0402 [SMD]"]
  C15 = Ceramic Capacitor [capacitance=0.05µF package="200 mil [THT, multilayer]"]
  C16 = Ceramic Capacitor [capacitance=250µF package="200 mil [THT, multilayer]"]
  SP1 = SPEAKER [package=pcb_mount_speaker]

nets (from the breadboard view):
  VDD: Part2.VCC, U1.3.3, Mod2.VDD, Mod3.VDD, C9.1, C14.0, C13.0, U3.V+
  GND: Part2.GND, U1.GND, Mod2.GND, Mod3.GND, C3.-, C4.-, Part3.negative, C9.0, JP1.3, C14.1, C13.1, C8.1, A1.Pin_3, U3.-IN, U3.V-, R2.Pin_0, SP1.+
  N1: Part2.SCL, U1.GPIO22
  N2: Part2.SDA, U1.GPIO21
  N3: Part2.INT, U1.GPIO23
  N4: U1.GPIO32, Mod2.Dir
  N5: U1.GPIO33, Mod2.Step
  N6: U1.GPIO25, Mod3.Dir
  N7: U1.GPIO26, Mod3.Step
  N8: U1.GPIO27, Mod2.MS2
  N9: U1.GPIO14, JP1.2
  N10: U1.GPIO12, JP1.8
  N11: U1.GPIO13, JP1.4
  N12: U1.VIN, JP1.1, C8.0, A1.Pin_4
  N13: U1.GPIO15, JP1.6
  N14: U1.GPIO4, Mod2.MS1
  N15: U1.GPIO16, Mod2.PDN2, Mod3.PDN2, R1.Pin_1
  N16: U1.GPIO17, R1.Pin_0
  N17: U1.GPIO5, Mod3.MS2
  N18: U1.GPIO18, Mod3.MS1
  N19: U1.GPIO19, Mod2.EN, Mod3.EN
  N20: U2.O, Mod2.VM, Mod3.VM, C3.+, C4.+, A1.Pin_2
  N21: U2.P, Part3.positive
  N22: M1.A, Mod2.A2
  N23: M1.C, Mod2.A1
  N24: M1.B, Mod2.B1
  N25: M1.D, Mod2.B2
  N26: Mod3.B2, M2.D
  N27: Mod3.B1, M2.B
  N28: Mod3.A1, M2.C
  N29: Mod3.A2, M2.A
  N30: U3.OUT, C15.0, C16.0
  N31: R2.Pin_1, C15.1
  N32: C16.1, SP1.-

custom parts:
  ESP32S-HiLetgo: HiLetgo ESP-WROOM-32 ESP32 ESP-32S Development Board 2.4GHz Dual-Mode WiFi + Bluetooth Dual Cores Microcontroller The ESP32 integrated with Antenna switches, RF Balun, power amplifiers, low-noise amplifiers, filters, and management modules, and the entire solution occupies the least area of PCB. 2.4 GHz Wi-Fi plus Bluetooth dual-mode chip, with TSMC Ultra-low power consumption 40nm technology,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
  TMC2209: TMC2209-LA stepper motor controller and driver. Supply voltage 4.75-28V Iphase up to 1.77A rms (2.5A peak)
  Lithium Ion Polymer Battery 3.7v 2500mAh: Lithium ion polymer (also known as 'lipo' or 'lipoly') batteries are thin, light and powerful. The output ranges from 4.2V when completely charged to 3.7V. This battery has a capacity of 2500mAh for a total of about 10 Wh. The batteries come pre-attached with a genuine 2-pin JST-PH connector as shown and include the necessary protection circuitry.
  MP2315: Ultra small module converts 4.5 – 24V input down to a 0.8 – 22V output @ up to 2A.
